# Fritzing sketch door open alarm (saved by Fritzing 0.9.3b)
breadboards: 1

parts:
  J1 = Piezo Speaker
  S1 = Reed switch [package=THT]
  Part1 = Arduino Uno (Rev3)
  LED1 = LED - 5mm [color="Red (633nm)" package="5 mm [THT]"]
  LED2 = LED - 5mm [color="Green (555nm)" package="5 mm [THT]"]
  R1 = Resistor [tolerance=±5% resistance=220 package=THT]
  R2 = Resistor [tolerance=±5% resistance=220 package=THT]
  R3 = Resistor [tolerance=±5% resistance=100 package=THT]
  R4 = Resistor [tolerance=±5% resistance=10k package=THT]

nets:
  N1: J1.pin1, Part1.GND, R1.Pin_0, R2.Pin_0, R4.Pin_0
  N2: J1.pin2, R3.Pin_0
  N3: S1.pin_1, Part1.D12/MISO, R4.Pin_1
  N4: S1.pin_2, Part1.5V
  N5: Part1.D9_PWM, R3.Pin_1
  N6: Part1.D10_PWM/SS, LED2.anode
  N7: Part1.D11_PWM/MOSI, LED1.anode
  N8: LED1.cathode, R1.Pin_1
  N9: LED2.cathode, R2.Pin_1
